// Logisim project lab10part1-fot3.circ as structural Verilog: 1 circuit, main circuit main
module main (
  input  [1:0] Read_Register_1,
  input  [1:0] Read_Register_2,
  input  [1:0] Write_Register,
  input  [15:0] Write_Data,
  output [15:0] out_5,
  output [15:0] out_6
);

  wire clock_1_out, demultiplexer_1_out0, demultiplexer_1_out1, demultiplexer_1_out2, demultiplexer_1_out3;
  wire [15:0] register_1_q, register_2_q, register_3_q, register_4_q;

  Demultiplexer #(.select(2)) demultiplexer_1 (
    .out0(demultiplexer_1_out0), .out1(demultiplexer_1_out1), .out2(demultiplexer_1_out2),
    .out3(demultiplexer_1_out3), .in(clock_1_out), .sel(Write_Register));  // open: en
  Clock clock_1 (.out(clock_1_out));
  Register #(.width(16), .trigger("falling")) register_1 (
    .D(Write_Data), .en(demultiplexer_1_out0), .Q(register_1_q), .clk(clock_1_out));  // open: clr
  Register #(.width(16), .trigger("falling")) register_2 (
    .D(Write_Data), .en(demultiplexer_1_out1), .Q(register_2_q), .clk(clock_1_out));  // open: clr
  Register #(.width(16), .trigger("falling")) register_3 (
    .D(Write_Data), .en(demultiplexer_1_out2), .Q(register_3_q), .clk(clock_1_out));  // open: clr
  Register #(.width(16), .trigger("falling")) register_4 (
    .D(Write_Data), .en(demultiplexer_1_out3), .Q(register_4_q), .clk(clock_1_out));  // open: clr
  Multiplexer #(.select(2), .width(16)) multiplexer_1 (
    .in0(register_1_q), .in1(register_2_q), .in2(register_3_q), .in3(register_4_q), .out(out_5),
    .sel(Read_Register_1));  // open: en
  Multiplexer #(.select(2), .width(16)) multiplexer_2 (
    .in0(register_1_q), .in1(register_2_q), .in2(register_3_q), .in3(register_4_q), .out(out_6),
    .sel(Read_Register_2));  // open: en
endmodule
