// Logisim project lab10part2-fot3.circ as structural Verilog: 1 circuit, main circuit main
module main (
);

  wire adder_1_out, and_1_out, clock_1_out, comparator_1_eq, controlled_buffer_1_out, not_1_out, not_2_out,
       not_3_out, register_1_q, RESET_out;
  wire [3:0] adder_2_out, ram_1_data, register_2_q;

  Clock clock_1 (.out(clock_1_out));
  not not_1 (not_1_out, register_1_q);
  assign controlled_buffer_1_out = not_2_out ? clock_1_out : 1'bz;  // Controlled_Buffer controlled_buffer_1
  not not_2 (not_2_out, and_1_out);
  Button RESET (.out(RESET_out));
  Adder #(.width(1)) adder_1 (.a(1'b1), .b(register_1_q), .out(adder_1_out));  // open: cin, cout
  RAM #(.addrWidth(4), .dataWidth(4)) ram_1 (
    .addr(register_2_q), .data(ram_1_data), .clk(controlled_buffer_1_out), .ld(not_1_out), .clr(RESET_out));  // open: sel
  Register #(.width(1)) register_1 (.D(adder_1_out), .Q(register_1_q), .clk(controlled_buffer_1_out));  // open: en, clr
  assign ram_1_data = register_1_q ? register_2_q : 4'bz;  // Controlled_Buffer controlled_buffer_2
  Register #(.width(4)) register_2 (.D(adder_2_out), .Q(register_2_q), .clk(register_1_q));  // open: en, clr
  Adder #(.width(4)) adder_2 (.a(ram_1_data), .b(4'b0001), .out(adder_2_out));  // open: cin, cout
  Comparator #(.width(4)) comparator_1 (.a(ram_1_data), .b(4'b1111), .eq(comparator_1_eq));  // open: gt, lt
  not not_3 (not_3_out, register_1_q);
  and and_1 (and_1_out, comparator_1_eq, not_3_out);
endmodule
