// Logisim project lab11partC-fot3.circ as structural Verilog: 3 circuits, main circuit main
module main (
  input  Input,
  output Output
);

  wire and_1_out, and_2_out, and_3_out, and_4_out, and_5_out, clock_1_out, d_ff_1_q, d_ff_2_q, not_1_out,
       not_2_out, not_3_out, not_4_out, not_5_out, not_6_out, or_1_out, or_2_out;

  not not_1 (not_1_out, d_ff_1_q);
  not not_2 (not_2_out, d_ff_2_q);
  not not_3 (not_3_out, d_ff_1_q);
  not not_4 (not_4_out, d_ff_2_q);
  not not_5 (not_5_out, d_ff_2_q);
  not not_6 (not_6_out, Input);
  and and_1 (and_1_out, not_1_out, d_ff_2_q, Input);
  and and_2 (and_2_out, d_ff_1_q, not_2_out);
  and and_3 (and_3_out, not_3_out, not_4_out, Input);
  and and_4 (and_4_out, d_ff_1_q, not_5_out, not_6_out);
  and and_5 (and_5_out, d_ff_1_q, d_ff_2_q, Input);
  or or_1 (or_1_out, and_1_out, and_2_out);
  Clock clock_1 (.out(clock_1_out));
  or or_2 (or_2_out, and_3_out, and_4_out, and_5_out);
  D_Flip_Flop d_ff_1 (.clk(clock_1_out), .D(or_1_out), .Q(d_ff_1_q));  // open: Qn, preset, en, reset
  D_Flip_Flop d_ff_2 (.clk(clock_1_out), .D(or_2_out), .Q(d_ff_2_q));  // open: Qn, preset, en, reset
  and and_6 (Output, d_ff_1_q, d_ff_2_q);
endmodule

module FSM (
  input  Input
);

  wire and_1_out, and_2_out, and_3_out, and_4_out, and_5_out, clock_1_out, d_ff_1_q, d_ff_2_q, not_1_out,
       not_2_out, not_3_out, not_4_out, not_5_out, not_6_out, or_1_out, or_2_out;

  not not_1 (not_1_out, d_ff_1_q);
  and and_1 (and_1_out, not_1_out, d_ff_2_q, Input);
  and and_2 (and_2_out, d_ff_1_q, not_2_out);
  not not_2 (not_2_out, d_ff_2_q);
  not not_3 (not_3_out, d_ff_1_q);
  not not_4 (not_4_out, d_ff_2_q);
  and and_3 (and_3_out, not_3_out, not_4_out, Input);
  not not_5 (not_5_out, d_ff_2_q);
  and and_4 (and_4_out, d_ff_1_q, not_5_out, not_6_out);
  not not_6 (not_6_out, Input);
  and and_5 (and_5_out, d_ff_1_q, d_ff_2_q, Input);
  or or_1 (or_1_out, and_1_out, and_2_out);
  Clock clock_1 (.out(clock_1_out));
  or or_2 (or_2_out, and_3_out, and_4_out, and_5_out);
  D_Flip_Flop d_ff_1 (.clk(clock_1_out), .D(or_1_out), .Q(d_ff_1_q));  // open: Qn, preset, en, reset
  D_Flip_Flop d_ff_2 (.clk(clock_1_out), .D(or_2_out), .Q(d_ff_2_q));  // open: Qn, preset, en, reset
endmodule

module Out (
  input  State_1,
  input  State_0,
  output Output
);

  and and_1 (Output, State_1, State_0);
endmodule
