// Logisim project lab08part3-fot3.circ as structural Verilog: 1 circuit, main circuit main
module main (
  input  B,
  input  C,
  input  A,
  output V
);

  wire AB_out, AC_out, BC_out, not_1_out, not_2_out, not_3_out;

  not not_1 (not_1_out, A);
  not not_2 (not_2_out, B);
  not not_3 (not_3_out, C);
  and AB (AB_out, not_1_out, not_2_out);
  and BC (BC_out, not_2_out, not_3_out);
  and AC (AC_out, not_1_out, not_3_out);
  or O1 (V, AB_out, AB_out, BC_out, AC_out, AC_out);
endmodule
