// Logisim project jrmips.circ as structural Verilog: 9 circuits, main circuit main
module main (
);

  wire alu_1_zero, clock_1_out, dispcontrol_1_dispupdate, halter_1_halt, maincontrol_1_ain,
       maincontrol_1_bin, maincontrol_1_memstr, maincontrol_1_regwrt, muldivcontrol_1_reg2enable, not_1_out;
  wire [1:0] maincontrol_1_brnchctrl, maincontrol_1_brsrc, maincontrol_1_imm, maincontrol_1_regsrc;
  wire [2:0] maincontrol_1_myop;
  wire [7:0] adder_1_out, and_1_out, multiplexer_1_out, multiplexer_2_out, PC_q, regfile_1_reg1;
  wire [15:0] alu_1_divrem, alu_1_multupper, alu_1_result, bit_extender_1_out, bit_extender_2_out,
       bit_extender_3_out, multiplexer_3_out, multiplexer_4_out, multiplexer_5_out, ram_1_data,
       regfile_1_reg2, register_1_q, rom_1_data;
  wire [15:8] regfile_1_reg1_2;

  not not_1 (not_1_out, halter_1_halt);
  Register #(.trigger("falling")) PC (.D(multiplexer_2_out), .en(not_1_out), .Q(PC_q), .clk(clock_1_out));  // open: clr
  Clock clock_1 (.out(clock_1_out));
  ROM #(.dataWidth(16)) rom_1 (.addr(PC_q), .data(rom_1_data));  // open: sel
  Adder adder_1 (.a(8'h1), .b(PC_q), .out(adder_1_out));  // open: cin, cout
  Multiplexer #(.width(8)) multiplexer_1 (
    .in0(adder_1_out), .in1(rom_1_data[8:1]), .out(multiplexer_1_out), .sel(alu_1_zero));  // open: en
  MulDivControl muldivcontrol_1 (.op(rom_1_data[15:12]), .Reg2Enable(muldivcontrol_1_reg2enable));
  Halter halter_1 (.func(rom_1_data[0]), .op(rom_1_data[15:12]), .halt(halter_1_halt));
  Multiplexer #(.select(2), .width(8)) multiplexer_2 (
    .in0(adder_1_out), .in1(multiplexer_1_out), .in2(rom_1_data[8:1]), .in3(regfile_1_reg1),
    .out(multiplexer_2_out), .sel(maincontrol_1_brsrc));  // open: en
  assign bit_extender_1_out = {{8{1'b0}}, rom_1_data[8:1]};  // Bit_Extender bit_extender_1
  assign bit_extender_2_out = {{8{rom_1_data[8]}}, rom_1_data[8:1]};  // Bit_Extender bit_extender_2
  MainControl maincontrol_1 (
    .subop(rom_1_data[0]), .op(rom_1_data[15:12]), .myop(maincontrol_1_myop), .imm(maincontrol_1_imm),
    .ain(maincontrol_1_ain), .bin(maincontrol_1_bin), .regwrt(maincontrol_1_regwrt),
    .memstr(maincontrol_1_memstr), .brsrc(maincontrol_1_brsrc), .regsrc(maincontrol_1_regsrc),
    .brnchctrl(maincontrol_1_brnchctrl));
  DispControl dispcontrol_1 (.subop(rom_1_data[0]), .op(rom_1_data[15:12]), .DispUpdate(dispcontrol_1_dispupdate));
  Multiplexer #(.select(2), .width(16)) multiplexer_3 (
    .in0(alu_1_result), .in1(bit_extender_2_out), .in2(ram_1_data), .in3(bit_extender_3_out),
    .out(multiplexer_3_out), .sel(maincontrol_1_regsrc));  // open: en
  RegFile regfile_1 (
    .Read_Register_1(rom_1_data[11:9]), .Read_Register_2(rom_1_data[8:6]), .Write_Register(rom_1_data[11:9]),
    .Write_Data(multiplexer_3_out), .MulDivData(multiplexer_5_out), .RegWrt(maincontrol_1_regwrt),
    .MulDiv(muldivcontrol_1_reg2enable), .Reg1({regfile_1_reg1_2, regfile_1_reg1}), .Reg2(regfile_1_reg2));
  Multiplexer #(.select(2), .width(16)) multiplexer_4 (
    .in0(regfile_1_reg2), .in1(bit_extender_1_out), .in2(bit_extender_2_out), .out(multiplexer_4_out),
    .sel(maincontrol_1_imm));  // open: in3, en
  assign bit_extender_3_out = {{8{1'b0}}, adder_1_out};  // Bit_Extender bit_extender_3
  Register #(.width(16), .trigger("falling")) register_1 (
    .D({regfile_1_reg1_2, regfile_1_reg1}), .en(dispcontrol_1_dispupdate), .Q(register_1_q), .clk(clock_1_out));  // open: clr
  assign and_1_out = regfile_1_reg2[7:0] & {8{1'b1}};  // AND_Gate and_1, 8 bits wide
  LED HALT (.in(halter_1_halt));
  Hex_Digit_Display hex_digit_display_1 (.value(register_1_q[11:8]));  // open: dp
  Hex_Digit_Display hex_digit_display_2 (.value(register_1_q[15:12]));  // open: dp
  RAM #(.dataWidth(16), .bus("separate")) ram_1 (
    .addr(and_1_out), .din({regfile_1_reg1_2, regfile_1_reg1}), .data(ram_1_data),
    .str(maincontrol_1_memstr), .clk(clock_1_out));  // open: sel, ld, clr
  Hex_Digit_Display hex_digit_display_3 (.value(register_1_q[7:4]));  // open: dp
  Hex_Digit_Display hex_digit_display_4 (.value(register_1_q[3:0]));  // open: dp
  ALU alu_1 (
    .A({regfile_1_reg1_2, regfile_1_reg1}), .Ainvert(maincontrol_1_ain), .B(multiplexer_4_out),
    .Binvert(maincontrol_1_bin), .OP(maincontrol_1_myop), .BranchControl(maincontrol_1_brnchctrl),
    .Result(alu_1_result), .MultUpper(alu_1_multupper), .Zero(alu_1_zero), .DivRem(alu_1_divrem));
  Multiplexer #(.width(16)) multiplexer_5 (
    .in0(alu_1_multupper), .in1(alu_1_divrem), .out(multiplexer_5_out), .sel(maincontrol_1_myop[0]));  // open: en

  // Notes on the sheet:
  //   Forbes Turley
  //   fot3@pitt.edu
endmodule

module RegFile (
  input  MulDiv,
  input  [2:0] Read_Register_1,
  input  [2:0] Read_Register_2,
  input  [2:0] Write_Register,
  input  RegWrt,
  input  [15:0] Write_Data,
  input  [15:0] MulDivData,
  output [15:0] Reg1,
  output [15:0] Reg2
);

  wire clock_1_out, demultiplexer_1_out0, demultiplexer_1_out1, demultiplexer_1_out2, demultiplexer_1_out3,
       demultiplexer_1_out4, demultiplexer_1_out5, demultiplexer_1_out6, demultiplexer_1_out7,
       demultiplexer_2_out0, demultiplexer_2_out1, demultiplexer_2_out2, demultiplexer_2_out3,
       demultiplexer_2_out4, demultiplexer_2_out5, demultiplexer_2_out6, demultiplexer_2_out7,
       demultiplexer_3_out0, demultiplexer_3_out1, demultiplexer_3_out2, demultiplexer_3_out3,
       demultiplexer_3_out4, demultiplexer_3_out5, demultiplexer_3_out6, demultiplexer_3_out7, or_1_out,
       or_2_out, or_3_out, or_4_out, or_5_out, or_6_out, or_7_out, or_8_out;
  wire [2:0] adder_1_out;
  wire [15:0] multiplexer_1_out, multiplexer_2_out, multiplexer_3_out, multiplexer_4_out, multiplexer_5_out,
       multiplexer_6_out, multiplexer_7_out, multiplexer_8_out, register_1_q, register_2_q, register_3_q,
       register_4_q, register_5_q, register_6_q, register_7_q, register_8_q;

  Adder #(.width(3)) adder_1 (.a(3'b001), .b(Write_Register), .out(adder_1_out));  // open: cin, cout
  Demultiplexer #(.select(3), .disabled(0)) demultiplexer_1 (
    .out0(demultiplexer_1_out0), .out1(demultiplexer_1_out1), .out2(demultiplexer_1_out2),
    .out3(demultiplexer_1_out3), .out4(demultiplexer_1_out4), .out5(demultiplexer_1_out5),
    .out6(demultiplexer_1_out6), .out7(demultiplexer_1_out7), .in(clock_1_out), .sel(Write_Register),
    .en(RegWrt));
  Demultiplexer #(.select(3), .disabled(0)) demultiplexer_2 (
    .out0(demultiplexer_2_out0), .out1(demultiplexer_2_out1), .out2(demultiplexer_2_out2),
    .out3(demultiplexer_2_out3), .out4(demultiplexer_2_out4), .out5(demultiplexer_2_out5),
    .out6(demultiplexer_2_out6), .out7(demultiplexer_2_out7), .in(clock_1_out), .sel(adder_1_out), .en(MulDiv));
  or or_1 (or_1_out, demultiplexer_1_out0, demultiplexer_2_out0);
  or or_2 (or_2_out, demultiplexer_1_out1, demultiplexer_2_out1);
  or or_3 (or_3_out, demultiplexer_1_out2, demultiplexer_2_out2);
  or or_4 (or_4_out, demultiplexer_1_out3, demultiplexer_2_out3);
  or or_5 (or_5_out, demultiplexer_1_out4, demultiplexer_2_out4);
  or or_6 (or_6_out, demultiplexer_1_out5, demultiplexer_2_out5);
  or or_7 (or_7_out, demultiplexer_1_out6, demultiplexer_2_out6);
  or or_8 (or_8_out, demultiplexer_1_out7, demultiplexer_2_out7);
  Demultiplexer #(.select(3), .disabled(0)) demultiplexer_3 (
    .out0(demultiplexer_3_out0), .out1(demultiplexer_3_out1), .out2(demultiplexer_3_out2),
    .out3(demultiplexer_3_out3), .out4(demultiplexer_3_out4), .out5(demultiplexer_3_out5),
    .out6(demultiplexer_3_out6), .out7(demultiplexer_3_out7), .in(clock_1_out), .sel(adder_1_out), .en(MulDiv));
  Multiplexer #(.width(16)) multiplexer_1 (
    .in0(Write_Data), .in1(MulDivData), .out(multiplexer_1_out), .sel(demultiplexer_3_out0));  // open: en
  Multiplexer #(.width(16)) multiplexer_2 (
    .in0(Write_Data), .in1(MulDivData), .out(multiplexer_2_out), .sel(demultiplexer_3_out1));  // open: en
  Multiplexer #(.width(16)) multiplexer_3 (
    .in0(Write_Data), .in1(MulDivData), .out(multiplexer_3_out), .sel(demultiplexer_3_out2));  // open: en
  Multiplexer #(.width(16)) multiplexer_4 (
    .in0(Write_Data), .in1(MulDivData), .out(multiplexer_4_out), .sel(demultiplexer_3_out3));  // open: en
  Multiplexer #(.width(16)) multiplexer_5 (
    .in0(Write_Data), .in1(MulDivData), .out(multiplexer_5_out), .sel(demultiplexer_3_out4));  // open: en
  Multiplexer #(.width(16)) multiplexer_6 (
    .in0(Write_Data), .in1(MulDivData), .out(multiplexer_6_out), .sel(demultiplexer_3_out5));  // open: en
  Multiplexer #(.width(16)) multiplexer_7 (
    .in0(Write_Data), .in1(MulDivData), .out(multiplexer_7_out), .sel(demultiplexer_3_out6));  // open: en
  Multiplexer #(.width(16)) multiplexer_8 (
    .in0(Write_Data), .in1(MulDivData), .out(multiplexer_8_out), .sel(demultiplexer_3_out7));  // open: en
  Clock clock_1 (.out(clock_1_out));
  Register #(.width(16), .trigger("falling")) register_1 (
    .D(multiplexer_1_out), .en(or_1_out), .Q(register_1_q), .clk(clock_1_out));  // open: clr
  Register #(.width(16), .trigger("falling")) register_2 (
    .D(multiplexer_2_out), .en(or_2_out), .Q(register_2_q), .clk(clock_1_out));  // open: clr
  Register #(.width(16), .trigger("falling")) register_3 (
    .D(multiplexer_3_out), .en(or_3_out), .Q(register_3_q), .clk(clock_1_out));  // open: clr
  Register #(.width(16), .trigger("falling")) register_4 (
    .D(multiplexer_4_out), .en(or_4_out), .Q(register_4_q), .clk(clock_1_out));  // open: clr
  Register #(.width(16), .trigger("falling")) register_5 (
    .D(multiplexer_5_out), .en(or_5_out), .Q(register_5_q), .clk(clock_1_out));  // open: clr
  Register #(.width(16), .trigger("falling")) register_6 (
    .D(multiplexer_6_out), .en(or_6_out), .Q(register_6_q), .clk(clock_1_out));  // open: clr
  Register #(.width(16), .trigger("falling")) register_7 (
    .D(multiplexer_7_out), .en(or_7_out), .Q(register_7_q), .clk(clock_1_out));  // open: clr
  Register #(.width(16), .trigger("falling")) register_8 (
    .D(multiplexer_8_out), .en(or_8_out), .Q(register_8_q), .clk(clock_1_out));  // open: clr
  Multiplexer #(.select(3), .width(16)) multiplexer_9 (
    .in0(register_1_q), .in1(register_2_q), .in2(register_3_q), .in3(register_4_q), .in4(register_5_q),
    .in5(register_6_q), .in6(register_7_q), .in7(register_8_q), .out(Reg1), .sel(Read_Register_1));  // open: en
  Multiplexer #(.select(3), .width(16)) multiplexer_10 (
    .in0(register_1_q), .in1(register_2_q), .in2(register_3_q), .in3(register_4_q), .in4(register_5_q),
    .in5(register_6_q), .in6(register_7_q), .in7(register_8_q), .out(Reg2), .sel(Read_Register_2));  // open: en
endmodule

module ALU (
  input  [15:0] A,
  input  Ainvert,
  input  [15:0] B,
  input  Binvert,
  input  [2:0] OP,
  input  [1:0] BranchControl,
  output [15:0] Result,
  output [15:0] MultUpper,
  output Zero,
  output [15:0] DivRem
);

  wire and_2_out, not_3_out, not_4_out, or_2_out;
  wire [15:0] adder_1_out, and_1_out, divider_1_out, multiplexer_1_out, multiplexer_2_out, multiplier_1_out,
       not_1_out, not_2_out, or_1_out, shifter_1_out, shifter_2_out;

  assign not_1_out = ~A;  // NOT_Gate not_1, 16 bits wide
  assign not_2_out = ~B;  // NOT_Gate not_2, 16 bits wide
  Multiplier #(.width(16)) multiplier_1 (.a(A), .b(B), .out(multiplier_1_out), .cout(MultUpper));  // open: cin
  Divider #(.width(16)) divider_1 (.a(A), .b(B), .out(divider_1_out), .rem(DivRem));  // open: upper
  Multiplexer #(.width(16)) multiplexer_1 (
    .in0(A), .in1(not_1_out), .out(multiplexer_1_out), .sel(Ainvert));  // open: en
  Multiplexer #(.width(16)) multiplexer_2 (
    .in0(B), .in1(not_2_out), .out(multiplexer_2_out), .sel(Binvert));  // open: en
  Adder #(.width(16)) adder_1 (
    .a(multiplexer_1_out), .b(multiplexer_2_out), .out(adder_1_out), .cin(Binvert));  // open: cout
  assign and_1_out = multiplexer_1_out & multiplexer_2_out;  // AND_Gate and_1, 16 bits wide
  assign or_1_out = multiplexer_1_out | multiplexer_2_out;  // OR_Gate or_1, 16 bits wide
  Shifter #(.width(16)) shifter_1 (.in(A), .\dist (B[3:0]), .out(shifter_1_out));
  Shifter #(.width(16), .shift("lr")) shifter_2 (.in(A), .\dist (B[3:0]), .out(shifter_2_out));
  Multiplexer #(.select(3), .width(16)) multiplexer_3 (
    .in0(and_1_out), .in1(or_1_out), .in2(adder_1_out), .in3({{15{1'b0}}, adder_1_out[15]}),
    .in4(multiplier_1_out), .in5(divider_1_out), .in6(shifter_1_out), .in7(shifter_2_out), .out(Result),
    .sel(OP));  // open: en
  not not_3 (not_3_out, A[15]);
  or or_2 (or_2_out, A[0], A[1], A[2], A[3], A[4], A[5], A[6], A[7], A[9], A[10], A[11], A[12], A[13], A[14], A[15], A[8]);
  not not_4 (not_4_out, or_2_out);
  and and_2 (and_2_out, or_2_out, not_3_out);
  Multiplexer #(.select(2)) multiplexer_4 (
    .in0(or_2_out), .in1(not_4_out), .in2(and_2_out), .in3(A[15]), .out(Zero), .sel(BranchControl));  // open: en
endmodule

module MainControl (
  input  [3:0] op,
  input  subop,
  output [2:0] myop,
  output [1:0] imm,
  output ain,
  output bin,
  output regwrt,
  output memstr,
  output [1:0] brsrc,
  output [1:0] regsrc,
  output [1:0] brnchctrl
);

  MainPt2 mainpt2_1 (
    .op3(op[3]), .op2(op[2]), .op1(op[1]), .op0(op[0]), .subop(subop), .myop2(myop[2]), .myop1(myop[1]),
    .myop0(myop[0]), .ainv(ain), .binv(bin), .imm1(imm[1]), .imm0(imm[0]), .regwrt(regwrt), .memstr(memstr));
  MainPt1 mainpt1_1 (
    .op0(op[0]), .op1(op[1]), .op2(op[2]), .op3(op[3]), .subop(subop), .brsrc0(brsrc[0]), .brsrc1(brsrc[1]),
    .regsrc0(regsrc[0]), .regsrc1(regsrc[1]), .brcntrll0(brnchctrl[0]), .brcntrl1(brnchctrl[1]));
endmodule

module MainPt1 (
  input  op0,
  input  op1,
  input  op2,
  input  op3,
  input  subop,
  output brsrc0,
  output brsrc1,
  output regsrc0,
  output regsrc1,
  output brcntrll0,
  output brcntrl1
);

  wire and_1_out, and_2_out, and_3_out, and_4_out, and_5_out, and_6_out, and_7_out, not_1_out, not_2_out,
       not_3_out, not_4_out, not_5_out;

  not not_1 (not_1_out, op1);
  not not_2 (not_2_out, op0);
  not not_3 (not_3_out, op1);
  not not_4 (not_4_out, op0);
  not not_5 (not_5_out, op1);
  and and_1 (and_1_out, op2, op1);
  and and_2 (and_2_out, op3, op0);
  not not_6 (brcntrl1, op0);
  and and_3 (and_3_out, op3, not_1_out, op0);
  and and_4 (and_4_out, op3, op1, not_2_out);
  and and_5 (and_5_out, op2, not_3_out, op0);
  and and_6 (and_6_out, op2, op1, not_4_out);
  and and_7 (and_7_out, op3, not_5_out, op0, subop);
  or or_1 (regsrc1, and_1_out, and_2_out);
  or or_2 (brsrc1, and_3_out, and_4_out);
  or or_3 (brsrc0, and_5_out, and_6_out, and_7_out);

  assign brcntrll0 = subop;
  assign regsrc0 = op3;
endmodule

module MainPt2 (
  input  op3,
  input  op2,
  input  op1,
  input  op0,
  input  subop,
  output myop2,
  output myop1,
  output myop0,
  output ainv,
  output binv,
  output imm1,
  output imm0,
  output regwrt,
  output memstr
);

  wire and_1_out, and_3_out, and_4_out, and_5_out, and_6_out, and_11_out, and_12_out, and_13_out, and_14_out,
       and_15_out, not_1_out, not_2_out, not_3_out, not_4_out, not_5_out, not_6_out, not_7_out, not_8_out,
       not_9_out, not_10_out, not_11_out, not_12_out, not_13_out, not_14_out, not_15_out, not_16_out,
       not_17_out, not_18_out, not_19_out, not_20_out, not_21_out, not_22_out;

  and and_1 (and_1_out, op1, op0);
  not not_1 (not_1_out, op1);
  not not_2 (not_2_out, op0);
  not not_3 (not_3_out, subop);
  not not_4 (not_4_out, op1);
  not not_5 (not_5_out, op0);
  not not_6 (not_6_out, op0);
  not not_7 (not_7_out, op1);
  not not_8 (not_8_out, subop);
  not not_9 (not_9_out, op1);
  not not_10 (not_10_out, op3);
  not not_11 (not_11_out, op2);
  not not_12 (not_12_out, op3);
  not not_13 (not_13_out, op1);
  not not_14 (not_14_out, op0);
  not not_15 (not_15_out, op2);
  not not_16 (not_16_out, op1);
  not not_17 (not_17_out, op0);
  not not_18 (not_18_out, op2);
  not not_19 (not_19_out, op1);
  not not_20 (not_20_out, subop);
  not not_21 (not_21_out, op3);
  not not_22 (not_22_out, subop);
  and and_2 (memstr, op2, op1, op0, subop);
  or or_1 (myop2, and_1_out, op2);
  and and_3 (and_3_out, not_1_out, op0);
  and and_4 (and_4_out, op1, not_2_out);
  and and_5 (and_5_out, op1, op0, not_3_out);
  and and_6 (and_6_out, op2, subop);
  and and_7 (ainv, not_4_out, not_5_out, subop);
  and and_8 (binv, not_6_out, subop);
  and and_9 (imm1, not_7_out, op0, not_8_out);
  and and_10 (imm0, not_9_out, op0, subop);
  and and_11 (and_11_out, not_10_out, not_11_out);
  and and_12 (and_12_out, not_12_out, not_13_out, not_14_out);
  and and_13 (and_13_out, not_15_out, not_16_out, not_17_out);
  and and_14 (and_14_out, not_18_out, not_19_out, not_20_out);
  and and_15 (and_15_out, not_21_out, op1, op0, not_22_out);
  or or_2 (myop1, and_3_out, and_4_out, op2);
  or or_3 (myop0, and_5_out, and_6_out);
  or or_4 (regwrt, and_11_out, and_12_out, and_13_out, and_14_out, and_15_out);
endmodule

module DispControl (
  input  [3:0] op,
  input  subop,
  output DispUpdate
);

  wire not_1_out, not_2_out;

  not not_1 (not_1_out, op[2]);
  not not_2 (not_2_out, subop);
  and and_1 (DispUpdate, op[3], not_1_out, op[1], op[0], not_2_out);
endmodule

module MulDivControl (
  input  [3:0] op,
  output Reg2Enable
);

  wire not_1_out, not_2_out;

  not not_1 (not_1_out, op[3]);
  not not_2 (not_2_out, op[2]);
  and and_1 (Reg2Enable, not_1_out, not_2_out, op[1], op[0]);
endmodule

module Halter (
  input  [3:0] op,
  input  func,
  output halt
);

  wire not_1_out;

  not not_1 (not_1_out, op[2]);
  and and_1 (halt, op[3], not_1_out, op[1], op[0], func);
endmodule
